// Logisim project EP1 (copy).circ as structural Verilog: 4 circuits, main circuit main
module main (
  input  [7:0] in_1,
  input  [7:0] in_2,
  input  in_3,
  output [7:0] out_4,
  output out_5,
  output out_6
);

  OP_Aritmetico_8bit op_aritmetico_8bit_1 (
    .A(in_1), .B(in_2), .OP(in_3), .R(out_4), .OvFlw_com_s(out_5), .OvFlw_sem_s(out_6));
endmodule

module Somador_1bit (
  input  a,
  input  b,
  input  c_in,
  output s,
  output c_out
);

  wire and_1_out, and_2_out, xor_1_out;

  xor xor_1 (xor_1_out, a, b);
  xor xor_2 (s, xor_1_out, c_in);
  and and_1 (and_1_out, c_in, xor_1_out);
  and and_2 (and_2_out, a, b);
  or or_1 (c_out, and_1_out, and_2_out);
endmodule

module Somador_8bit (
  input  [7:0] A,
  input  [7:0] B,
  input  c_in_0,
  output [7:0] R,
  output c_out_7,
  output c_out_8
);

  wire somador_1bit_1_c_out, somador_1bit_2_c_out, somador_1bit_3_c_out, somador_1bit_4_c_out,
       somador_1bit_5_c_out, somador_1bit_6_c_out, xor_1_out, xor_2_out, xor_3_out, xor_4_out, xor_5_out,
       xor_6_out, xor_7_out, xor_8_out;

  xor xor_1 (xor_1_out, B[0], c_in_0);
  xor xor_2 (xor_2_out, B[1], c_in_0);
  xor xor_3 (xor_3_out, B[2], c_in_0);
  xor xor_4 (xor_4_out, B[3], c_in_0);
  xor xor_5 (xor_5_out, B[4], c_in_0);
  xor xor_6 (xor_6_out, B[5], c_in_0);
  xor xor_7 (xor_7_out, B[6], c_in_0);
  xor xor_8 (xor_8_out, B[7], c_in_0);
  Somador_1bit somador_1bit_1 (.a(A[0]), .b(xor_1_out), .c_in(c_in_0), .s(R[0]), .c_out(somador_1bit_1_c_out));
  Somador_1bit somador_1bit_2 (
    .a(A[1]), .b(xor_2_out), .c_in(somador_1bit_1_c_out), .s(R[1]), .c_out(somador_1bit_2_c_out));
  Somador_1bit somador_1bit_3 (
    .a(A[2]), .b(xor_3_out), .c_in(somador_1bit_2_c_out), .s(R[2]), .c_out(somador_1bit_3_c_out));
  Somador_1bit somador_1bit_4 (
    .a(A[3]), .b(xor_4_out), .c_in(somador_1bit_3_c_out), .s(R[3]), .c_out(somador_1bit_4_c_out));
  Somador_1bit somador_1bit_5 (
    .a(A[4]), .b(xor_5_out), .c_in(somador_1bit_4_c_out), .s(R[4]), .c_out(somador_1bit_5_c_out));
  Somador_1bit somador_1bit_6 (
    .a(A[5]), .b(xor_6_out), .c_in(somador_1bit_5_c_out), .s(R[5]), .c_out(somador_1bit_6_c_out));
  Somador_1bit somador_1bit_7 (.a(A[6]), .b(xor_7_out), .c_in(somador_1bit_6_c_out), .s(R[6]), .c_out(c_out_7));
  Somador_1bit somador_1bit_8 (.a(A[7]), .b(xor_8_out), .c_in(c_out_7), .s(R[7]), .c_out(c_out_8));
endmodule

module OP_Aritmetico_8bit (
  input  [7:0] A,
  input  [7:0] B,
  input  OP,
  output [7:0] R,
  output OvFlw_com_s,
  output OvFlw_sem_s
);

  wire somador_8bit_1_c_out_7, somador_8bit_1_c_out_8;

  Somador_8bit somador_8bit_1 (
    .A(A), .B(B), .c_in_0(OP), .R(R), .c_out_7(somador_8bit_1_c_out_7), .c_out_8(somador_8bit_1_c_out_8));
  xor xor_1 (OvFlw_com_s, somador_8bit_1_c_out_7, somador_8bit_1_c_out_8);
  xor xor_2 (OvFlw_sem_s, somador_8bit_1_c_out_8, OP);
endmodule
