// Logisim project ULA.circ as structural Verilog: 7 circuits, main circuit main
module main (
  input  [7:0] in_1,
  input  [7:0] in_2,
  input  in_3,
  output [7:0] out_4,
  output out_5,
  output out_6,
  output out_7,
  output out_8,
  output out_9,
  output out_10,
  output out_11,
  output out_12
);

  ULA ula_1 (
    .A(in_1), .B(in_2), .OP(in_3), .R(out_4), .o1(out_5), .o2(out_6), .c0(out_7), .c1(out_8), .c2(out_9),
    .c3(out_10), .c4(out_11), .c5(out_12));
endmodule

module Comp_1bit (
  input  A,
  input  B,
  output A_maior,
  output Iguais,
  output B_maior
);

  wire not_1_out, not_2_out, not_3_out, xor_1_out;

  and and_1 (A_maior, A, not_1_out);
  not not_1 (not_1_out, B);
  xor xor_1 (xor_1_out, A, B);
  not not_2 (not_2_out, A_maior);
  not not_3 (not_3_out, xor_1_out);
  and and_2 (Iguais, not_2_out, not_3_out);
  nor nor_1 (B_maior, Iguais, A_maior);
endmodule

module Comp_8bit (
  input  [7:0] A,
  input  [7:0] B,
  output c0,
  output c1,
  output c2,
  output c3,
  output c4,
  output c5
);

  wire and_1_out, and_2_out, and_3_out, and_4_out, and_5_out, and_6_out, and_7_out, comp_1bit_1_a_maior,
       comp_1bit_1_iguais, comp_1bit_2_a_maior, comp_1bit_2_iguais, comp_1bit_3_a_maior, comp_1bit_3_iguais,
       comp_1bit_4_a_maior, comp_1bit_4_iguais, comp_1bit_5_a_maior, comp_1bit_5_iguais, comp_1bit_6_a_maior,
       comp_1bit_6_iguais, comp_1bit_7_a_maior, comp_1bit_7_iguais, comp_1bit_8_a_maior, comp_1bit_8_b_maior,
       comp_1bit_8_iguais, or_1_out, or_2_out, or_3_out, or_4_out, or_5_out, or_6_out;

  Comp_1bit comp_1bit_1 (
    .A(A[0]), .B(B[0]), .A_maior(comp_1bit_1_a_maior), .Iguais(comp_1bit_1_iguais));  // open: B_maior
  Comp_1bit comp_1bit_2 (
    .A(A[1]), .B(B[1]), .A_maior(comp_1bit_2_a_maior), .Iguais(comp_1bit_2_iguais));  // open: B_maior
  Comp_1bit comp_1bit_3 (
    .A(A[2]), .B(B[2]), .A_maior(comp_1bit_3_a_maior), .Iguais(comp_1bit_3_iguais));  // open: B_maior
  Comp_1bit comp_1bit_4 (
    .A(A[3]), .B(B[3]), .A_maior(comp_1bit_4_a_maior), .Iguais(comp_1bit_4_iguais));  // open: B_maior
  Comp_1bit comp_1bit_5 (
    .A(A[4]), .B(B[4]), .A_maior(comp_1bit_5_a_maior), .Iguais(comp_1bit_5_iguais));  // open: B_maior
  Comp_1bit comp_1bit_6 (
    .A(A[5]), .B(B[5]), .A_maior(comp_1bit_6_a_maior), .Iguais(comp_1bit_6_iguais));  // open: B_maior
  Comp_1bit comp_1bit_7 (
    .A(A[6]), .B(B[6]), .A_maior(comp_1bit_7_a_maior), .Iguais(comp_1bit_7_iguais));  // open: B_maior
  Comp_1bit comp_1bit_8 (
    .A(A[7]), .B(B[7]), .A_maior(comp_1bit_8_a_maior), .Iguais(comp_1bit_8_iguais),
    .B_maior(comp_1bit_8_b_maior));
  and and_1 (and_1_out, comp_1bit_1_a_maior, comp_1bit_2_iguais);
  or or_1 (or_1_out, and_1_out, comp_1bit_2_a_maior);
  and and_2 (and_2_out, or_1_out, comp_1bit_3_iguais);
  or or_2 (or_2_out, and_2_out, comp_1bit_3_a_maior);
  and and_3 (and_3_out, or_2_out, comp_1bit_4_iguais);
  or or_3 (or_3_out, and_3_out, comp_1bit_4_a_maior);
  and and_4 (and_4_out, or_3_out, comp_1bit_5_iguais);
  or or_4 (or_4_out, and_4_out, comp_1bit_5_a_maior);
  and and_5 (and_5_out, or_4_out, comp_1bit_6_iguais);
  or or_5 (or_5_out, and_5_out, comp_1bit_6_a_maior);
  and and_6 (and_6_out, or_5_out, comp_1bit_7_iguais);
  or or_6 (or_6_out, and_6_out, comp_1bit_7_a_maior);
  and and_7 (and_7_out, or_6_out, comp_1bit_8_iguais);
  or or_7 (c0, and_7_out, comp_1bit_8_a_maior);
  or or_8 (c4, comp_1bit_8_b_maior, and_7_out);
  and and_8 (c2, comp_1bit_1_iguais, comp_1bit_2_iguais, comp_1bit_3_iguais, comp_1bit_4_iguais, comp_1bit_5_iguais, comp_1bit_6_iguais, comp_1bit_7_iguais, comp_1bit_8_iguais);
  nor nor_1 (c3, A[0], A[1], A[2], A[3], A[4], A[5], A[6], A[7]);
  nor nor_2 (c1, c0, c2);
  nor nor_3 (c5, c4, c2);
endmodule

module Somador_1bit (
  input  a,
  input  b,
  input  c_in,
  output s,
  output c_out
);

  wire and_1_out, and_2_out, xor_1_out;

  xor xor_1 (xor_1_out, a, b);
  xor xor_2 (s, xor_1_out, c_in);
  and and_1 (and_1_out, c_in, xor_1_out);
  and and_2 (and_2_out, a, b);
  or or_1 (c_out, and_1_out, and_2_out);
endmodule

module Somador_8bit (
  input  [7:0] A,
  input  [7:0] B,
  input  c_in_0,
  output [7:0] R,
  output c_out_7,
  output c_out_8
);

  wire somador_1bit_1_c_out, somador_1bit_2_c_out, somador_1bit_3_c_out, somador_1bit_4_c_out,
       somador_1bit_5_c_out, somador_1bit_6_c_out, xor_1_out, xor_2_out, xor_3_out, xor_4_out, xor_5_out,
       xor_6_out, xor_7_out, xor_8_out;

  xor xor_1 (xor_1_out, B[0], c_in_0);
  xor xor_2 (xor_2_out, B[1], c_in_0);
  xor xor_3 (xor_3_out, B[2], c_in_0);
  xor xor_4 (xor_4_out, B[3], c_in_0);
  xor xor_5 (xor_5_out, B[4], c_in_0);
  xor xor_6 (xor_6_out, B[5], c_in_0);
  xor xor_7 (xor_7_out, B[6], c_in_0);
  xor xor_8 (xor_8_out, B[7], c_in_0);
  Somador_1bit somador_1bit_1 (.a(A[0]), .b(xor_1_out), .c_in(c_in_0), .s(R[0]), .c_out(somador_1bit_1_c_out));
  Somador_1bit somador_1bit_2 (
    .a(A[1]), .b(xor_2_out), .c_in(somador_1bit_1_c_out), .s(R[1]), .c_out(somador_1bit_2_c_out));
  Somador_1bit somador_1bit_3 (
    .a(A[2]), .b(xor_3_out), .c_in(somador_1bit_2_c_out), .s(R[2]), .c_out(somador_1bit_3_c_out));
  Somador_1bit somador_1bit_4 (
    .a(A[3]), .b(xor_4_out), .c_in(somador_1bit_3_c_out), .s(R[3]), .c_out(somador_1bit_4_c_out));
  Somador_1bit somador_1bit_5 (
    .a(A[4]), .b(xor_5_out), .c_in(somador_1bit_4_c_out), .s(R[4]), .c_out(somador_1bit_5_c_out));
  Somador_1bit somador_1bit_6 (
    .a(A[5]), .b(xor_6_out), .c_in(somador_1bit_5_c_out), .s(R[5]), .c_out(somador_1bit_6_c_out));
  Somador_1bit somador_1bit_7 (.a(A[6]), .b(xor_7_out), .c_in(somador_1bit_6_c_out), .s(R[6]), .c_out(c_out_7));
  Somador_1bit somador_1bit_8 (.a(A[7]), .b(xor_8_out), .c_in(c_out_7), .s(R[7]), .c_out(c_out_8));
endmodule

module OP_Aritmetico_8bit (
  input  [7:0] A,
  input  [7:0] B,
  input  OP,
  output [7:0] R,
  output OvFlw_com_s,
  output OvFlw_sem_s
);

  wire somador_8bit_1_c_out_7, somador_8bit_1_c_out_8;

  Somador_8bit somador_8bit_1 (
    .A(A), .B(B), .c_in_0(OP), .R(R), .c_out_7(somador_8bit_1_c_out_7), .c_out_8(somador_8bit_1_c_out_8));
  xor xor_1 (OvFlw_com_s, somador_8bit_1_c_out_7, somador_8bit_1_c_out_8);
  xor xor_2 (OvFlw_sem_s, somador_8bit_1_c_out_8, OP);
endmodule

module ULA (
  input  [7:0] A,
  input  [7:0] B,
  input  OP,
  output [7:0] R,
  output o1,
  output o2,
  output c0,
  output c1,
  output c2,
  output c3,
  output c4,
  output c5
);

  OP_Aritmetico_8bit op_aritmetico_8bit_1 (.A(A), .B(B), .OP(OP), .R(R), .OvFlw_com_s(o2), .OvFlw_sem_s(o1));
  Comp_8bit comp_8bit_1 (.A(A), .B(B), .c0(c0), .c1(c1), .c2(c2), .c3(c3), .c4(c4), .c5(c5));
endmodule
